# Fritzing sketch Final Project Fritzing (saved by Fritzing 0.7.12b)
breadboards: 1

parts:
  J1 = Basic Servo
  VCC1 = Battery block 9V
  Arduino1 = Arduino
  R1 = Photocell (LDR) [package=THT]
  R2 = 10k Ω Resistor [package=THT]
  R3 = Trimmer Potentiometer [package=THT]  # not connected

nets:
  GND: J1.gnd, VCC1.-, Arduino1.GND, R2.Pin_0
  N1: J1.vcc, VCC1.+
  N2: J1.pulse, Arduino1.D7
  N3: Arduino1.+5V, R1.pin_1
  N4: Arduino1.A0, R1.pin_0, R2.Pin_1
